// Logisim project CRC.circ as structural Verilog: 2 circuits, main circuit CRC
module \四位  (
  input  [3:0] \被除数 ,
  input  [3:0] \除数 ,
  output [2:0] \C_3位余数 ,
  output \D_一位商 
);

  wire [3:0] multiplexer_1_out, xor_1_out;

  assign xor_1_out = \被除数  ^ \除数 ;  // XOR_Gate xor_1, 4 bits wide
  // Probe on multiplexer_1_out
  Multiplexer #(.width(4)) multiplexer_1 (
    .in0(\被除数 ), .in1(xor_1_out), .out(multiplexer_1_out), .sel(\被除数 [3]));  // open: en
  Bit_Extender #(.in_width(4), .out_width(3)) bit_extender_1 (.in(multiplexer_1_out), .out(\C_3位余数 ));

  assign \D_一位商  = \被除数 [3];

  // Other names for the same wires on the sheet: A[3:0] = \被除数 ; slt = \被除数 [3]; B[3:0] = \除数 
endmodule

module CRC (
  input  [3:0] \B四位除数 ,
  input  [7:0] \A原数据 ,
  output [10:0] out_3
);

  wire [2:0] \四位_1_c_3位余数 , \四位_2_c_3位余数 , \四位_3_c_3位余数 , \四位_4_c_3位余数 , \四位_5_c_3位余数 , \四位_6_c_3位余数 ,
       \四位_7_c_3位余数 ;

  // Probe on \A原数据 [7:4]
  // Probe on {\A原数据 , 3'b000}
  \四位  \u_四位_1  (.\被除数 (\A原数据 [7:4]), .\除数 (\B四位除数 ), .\C_3位余数 (\四位_1_c_3位余数 ));  // open: D_一位商
  // Probe on {\四位_1_c_3位余数 , \A原数据 [3]}
  \四位  \u_四位_2  (.\被除数 ({\四位_1_c_3位余数 , \A原数据 [3]}), .\除数 (\B四位除数 ), .\C_3位余数 (\四位_2_c_3位余数 ));  // open: D_一位商
  \四位  \u_四位_3  (.\被除数 ({\四位_2_c_3位余数 , \A原数据 [2]}), .\除数 (\B四位除数 ), .\C_3位余数 (\四位_3_c_3位余数 ));  // open: D_一位商
  // Probe on {\四位_2_c_3位余数 , \A原数据 [2]}
  // Probe on {\四位_3_c_3位余数 , \A原数据 [1]}
  \四位  \u_四位_4  (.\被除数 ({\四位_3_c_3位余数 , \A原数据 [1]}), .\除数 (\B四位除数 ), .\C_3位余数 (\四位_4_c_3位余数 ));  // open: D_一位商
  \四位  \u_四位_5  (.\被除数 ({\四位_4_c_3位余数 , \A原数据 [0]}), .\除数 (\B四位除数 ), .\C_3位余数 (\四位_5_c_3位余数 ));  // open: D_一位商
  // Probe on {\四位_4_c_3位余数 , \A原数据 [0]}
  // Probe on {\四位_5_c_3位余数 , 1'b0}
  \四位  \u_四位_6  (.\被除数 ({\四位_5_c_3位余数 , 1'b0}), .\除数 (\B四位除数 ), .\C_3位余数 (\四位_6_c_3位余数 ));  // open: D_一位商
  \四位  \u_四位_7  (.\被除数 ({\四位_6_c_3位余数 , 1'b0}), .\除数 (\B四位除数 ), .\C_3位余数 (\四位_7_c_3位余数 ));  // open: D_一位商
  // Probe on {\四位_6_c_3位余数 , 1'b0}
  \四位  \u_四位_8  (.\被除数 ({\四位_7_c_3位余数 , 1'b0}), .\除数 (\B四位除数 ), .\C_3位余数 (out_3[2:0]));  // open: D_一位商

  assign out_3[10:3] = \A原数据 ;

  // Other names for the same wires on the sheet: a6 = \A原数据 [3]; a5 = \A原数据 [2]; a4 = \A原数据 [1]; a3 = \A原数据 [0];
  //   ans[2:0] = out_3[2:0]; a7 = \A原数据 [4]; a8 = \A原数据 [5]; a9 = \A原数据 [6]; a10 = \A原数据 [7]; 除数[3:0] = \B四位除数 
endmodule
