// Logisim project P3.circ as structural Verilog: 9 circuits, main circuit main
module main (
  input  in_1,
  output [31:0] out_2,
  output [31:0] out_3,
  output out_4,
  output [4:0] out_5,
  output [31:0] out_6,
  output out_7,
  output [31:0] out_8,
  output [31:0] out_9
);

  wire Bsel, clk, EXTOp, zero;
  wire [1:0] A3Sel, WDSel;
  wire [2:0] ALUop, NPCOp;
  wire [31:0] dm_1_rd, ext_1_out_3, grf_1_rd1, multiplexer_3_out, npc_1_npc, npc_1_pc_4;

  Clock clock_1 (.out(clk));
  PC pc_1 (.in_1(in_1), .in(npc_1_npc), .out(out_3), .in_2(clk));
  NPC npc_1 (
    .pc(out_3), .imm16(out_2[15:0]), .ra(grf_1_rd1), .zero(zero), .PC_4(npc_1_pc_4), .NPC(npc_1_npc),
    .NPCOp(NPCOp));
  IM im_1 (.PC(out_3), .out_2(out_2));
  // Probe on out_2[25:21]
  // Probe on A3Sel
  Multiplexer #(.select(2), .width(5)) multiplexer_1 (
    .in0(out_2[20:16]), .in1(out_2[15:11]), .in2({5{1'b1}}), .out(out_5), .sel(A3Sel));  // open: in3, en
  Multiplexer #(.select(2), .width(32)) multiplexer_2 (
    .in0(out_8), .in1(dm_1_rd), .in2(npc_1_pc_4), .out(out_6), .sel(WDSel));  // open: in3, en
  GRF grf_1 (
    .A1(out_2[25:21]), .A2(out_2[20:16]), .A3(out_5), .wd(out_6), .RD1(grf_1_rd1), .RD2(out_9), .clk(clk),
    .reset(in_1), .WE(out_4));
  // Probe on WDSel
  EXT ext_1 (.in_1(out_2[15:0]), .extOp(EXTOp), .out_3(ext_1_out_3));
  ctrl ctrl_1 (
    .Op(out_2[31:26]), .func(out_2[5:0]), .ALUOp(ALUop), .RFwr(out_4), .Bsel(Bsel), .ExtOp(EXTOp),
    .A3sel(A3Sel), .WDsel(WDSel), .NPCop(NPCOp), .DMWr(out_7));  // open: beq, j_jal, jal, jr
  Multiplexer #(.width(32)) multiplexer_3 (
    .in0(out_9), .in1(ext_1_out_3), .out(multiplexer_3_out), .sel(Bsel));  // open: en
  ALU alu_1 (.ALUOp(ALUop), .Zero(zero), .ALUout(out_8), .RD1(grf_1_rd1), .RD2(multiplexer_3_out));
  DM dm_1 (.addr(out_8), .WD(out_9), .RD(dm_1_rd), .in_1(out_7), .in_2(in_1), .in_3(clk));

  // Other names for the same wires on the sheet: DMWr = out_7; func[5:0] = out_2[5:0]; imm16[15:0] = out_2[15:0];
  //   imm26[25:0] = out_2[25:0]; instr[31:0] = out_2; shamt[4:0] = out_2[10:6]; Rd[4:0] = out_2[15:11];
  //   Rt[4:0] = out_2[20:16]; Rs[4:0] = out_2[25:21]; op[5:0] = out_2[31:26]; MemAddr[31:0] = out_8;
  //   MemData[31:0] = out_9; pc[31:0] = out_3; RegAddr[4:0] = out_5; RegData[31:0] = out_6; reset = in_1;
  //   RFWr = out_4

  // Notes on the sheet:
  //   非R型
endmodule

module GRF (
  input  clk,
  input  reset,
  input  WE,
  input  [4:0] A1,
  input  [4:0] A2,
  input  [4:0] A3,
  input  [31:0] wd,
  output [31:0] RD1,
  output [31:0] RD2
);

  wire [31:0] _0, _1, _2, _3, _4, _5, _6, _7, _8, _9, _10, _11, _12, _13, _14, _15, _16, _17, _18, _19, _20,
       _21, _22, _23, _24, _25, _26, _27, _28, _29, _30, _31, o1, o2, o3, o4, o5, o6, o7, o8, o9, o10, o11,
       o12, o13, o14, o15, o16, o17, o18, o19, o20, o21, o22, o23, o24, o25, o26, o27, o28, o29, o30, o31;

  Demultiplexer #(.select(5), .width(32), .tristate("true")) demultiplexer_1 (
    .out1(_1), .out2(_2), .out3(_3), .out4(_4), .out5(_5), .out6(_6), .out7(_7), .out8(_8), .out9(_9),
    .out10(_10), .out11(_11), .out12(_12), .out13(_13), .out14(_14), .out15(_15), .out16(_16), .out17(_17),
    .out18(_18), .out19(_19), .out20(_20), .out21(_21), .out22(_22), .out23(_23), .out24(_24), .out25(_25),
    .out26(_26), .out27(_27), .out28(_28), .out29(_29), .out30(_30), .out31(_31), .in(wd), .sel(A3));  // open: out0, en
  Register #(.width(32)) register_1 (.D({32{1'b0}}), .en(WE), .Q(_0), .clk(clk), .clr(reset));
  Register #(.width(32)) R01 (.D(_1), .en(WE), .Q(o1), .clk(clk), .clr(reset));
  Register #(.width(32)) register_2 (.D(_6), .en(WE), .Q(o6), .clk(clk), .clr(reset));
  Register #(.width(32)) register_3 (.D(_11), .en(WE), .Q(o11), .clk(clk), .clr(reset));
  Register #(.width(32)) register_4 (.D(_16), .en(WE), .Q(o16), .clk(clk), .clr(reset));
  Register #(.width(32)) register_5 (.D(_21), .en(WE), .Q(o21), .clk(clk), .clr(reset));
  Register #(.width(32)) register_6 (.D(_26), .en(WE), .Q(o26), .clk(clk), .clr(reset));
  Register #(.width(32)) register_7 (.D(_31), .en(WE), .Q(o31), .clk(clk), .clr(reset));
  Register #(.width(32)) register_8 (.D(_2), .en(WE), .Q(o2), .clk(clk), .clr(reset));
  Register #(.width(32)) register_9 (.D(_7), .en(WE), .Q(o7), .clk(clk), .clr(reset));
  Register #(.width(32)) register_10 (.D(_12), .en(WE), .Q(o12), .clk(clk), .clr(reset));
  Register #(.width(32)) register_11 (.D(_17), .en(WE), .Q(o17), .clk(clk), .clr(reset));
  Register #(.width(32)) register_12 (.D(_22), .en(WE), .Q(o22), .clk(clk), .clr(reset));
  Register #(.width(32)) register_13 (.D(_27), .en(WE), .Q(o27), .clk(clk), .clr(reset));
  Register #(.width(32)) register_14 (.D(_3), .en(WE), .Q(o3), .clk(clk), .clr(reset));
  Register #(.width(32)) register_15 (.D(_18), .en(WE), .Q(o18), .clk(clk), .clr(reset));
  Register #(.width(32)) register_16 (.D(_23), .en(WE), .Q(o23), .clk(clk), .clr(reset));
  Register #(.width(32)) register_17 (.D(_28), .en(WE), .Q(o28), .clk(clk), .clr(reset));
  Register #(.width(32)) register_18 (.D(_8), .en(WE), .Q(o8), .clk(clk), .clr(reset));
  Register #(.width(32)) register_19 (.D(_13), .en(WE), .Q(o13), .clk(clk), .clr(reset));
  Register #(.width(32)) register_20 (.D(_4), .en(WE), .Q(o4), .clk(clk), .clr(reset));
  Register #(.width(32)) register_21 (.D(_9), .en(WE), .Q(o9), .clk(clk), .clr(reset));
  Register #(.width(32)) register_22 (.D(_14), .en(WE), .Q(o14), .clk(clk), .clr(reset));
  Register #(.width(32)) register_23 (.D(_19), .en(WE), .Q(o19), .clk(clk), .clr(reset));
  Register #(.width(32)) register_24 (.D(_24), .en(WE), .Q(o24), .clk(clk), .clr(reset));
  Register #(.width(32)) register_25 (.D(_29), .en(WE), .Q(o29), .clk(clk), .clr(reset));
  Register #(.width(32)) register_26 (.D(_5), .en(WE), .Q(o5), .clk(clk), .clr(reset));
  Register #(.width(32)) register_27 (.D(_10), .en(WE), .Q(o10), .clk(clk), .clr(reset));
  Register #(.width(32)) register_28 (.D(_15), .en(WE), .Q(o15), .clk(clk), .clr(reset));
  Register #(.width(32)) register_29 (.D(_20), .en(WE), .Q(o20), .clk(clk), .clr(reset));
  Register #(.width(32)) register_30 (.D(_25), .en(WE), .Q(o25), .clk(clk), .clr(reset));
  Register #(.width(32)) register_31 (.D(_30), .en(WE), .Q(o30), .clk(clk), .clr(reset));
  Multiplexer #(.select(5), .width(32)) multiplexer_1 (
    .in0(_0), .in1(o1), .in2(o2), .in3(o3), .in4(o4), .in5(o5), .in6(o6), .in7(o7), .in8(o8), .in9(o9),
    .in10(o10), .in11(o11), .in12(o12), .in13(o13), .in14(o14), .in15(o15), .in16(o16), .in17(o17),
    .in18(o18), .in19(o19), .in20(o20), .in21(o21), .in22(o22), .in23(o23), .in24(o24), .in25(o25),
    .in26(o26), .in27(o27), .in28(o28), .in29(o29), .in30(o30), .in31(o31), .out(RD1), .sel(A1));  // open: en
  Multiplexer #(.select(5), .width(32)) multiplexer_2 (
    .in0(_0), .in1(o1), .in2(o2), .in3(o3), .in4(o4), .in5(o5), .in6(o6), .in7(o7), .in8(o8), .in9(o9),
    .in10(o10), .in11(o11), .in12(o12), .in13(o13), .in14(o14), .in15(o15), .in16(o16), .in17(o17),
    .in18(o18), .in19(o19), .in20(o20), .in21(o21), .in22(o22), .in23(o23), .in24(o24), .in25(o25),
    .in26(o26), .in27(o27), .in28(o28), .in29(o29), .in30(o30), .in31(o31), .out(RD2), .sel(A2));  // open: en
endmodule

module NPC (
  input  [31:0] pc,
  input  [15:0] imm16,
  input  [31:0] ra,
  input  [2:0] NPCOp,
  input  zero,
  output [31:0] PC_4,
  output [31:0] NPC
);

  wire beq, comparator_1_eq;
  wire [31:0] beqAddr, bit_extender_1_out, multiplexer_1_out;

  Comparator #(.width(3), .mode("unsigned")) comparator_1 (
    .a(NPCOp), .b(3'b001), .eq(comparator_1_eq));  // open: gt, lt
  Adder #(.width(32)) adder_1 (.a(pc), .b(32'h4), .out(PC_4));  // open: cin, cout
  assign bit_extender_1_out = {{14{imm16[15]}}, {imm16, 2'b00}};  // Bit_Extender bit_extender_1
  Adder #(.width(32)) adder_2 (.a(PC_4), .b(bit_extender_1_out), .out(beqAddr));  // open: cin, cout
  and and_1 (beq, comparator_1_eq, zero);
  Multiplexer #(.width(32)) multiplexer_1 (.in0(PC_4), .in1(beqAddr), .out(multiplexer_1_out), .sel(beq));  // open: en
  Multiplexer #(.select(3), .width(32)) multiplexer_2 (
    .in0(PC_4), .in1(multiplexer_1_out), .out(NPC), .sel(NPCOp));  // open: in2, in3, in4, in5, in6, in7, en
endmodule

module IM (
  input  [31:0] PC,
  output [31:0] out_2
);

  wire [31:0] subtractor_1_out;

  Subtractor #(.width(32)) subtractor_1 (.a(PC), .b(32'h3000), .out(subtractor_1_out));  // open: bin, bout
  ROM #(.addrWidth(12), .dataWidth(32)) rom_1 (.addr(subtractor_1_out[13:2]), .data(out_2));  // open: sel

  // Notes on the sheet:
  //   contents of rom_1 (hex, n*v repeats v):
  //   341c0000 341d0000 34013456 210820 8c010004 ac010004 3c027878 411822 3c051234 34040005 0 ac85ffff
  //   8c83ffff 10650001 1000000d 34670404 10e3000b 0 3c087777 3508ffff 80022 34001100 e65020 34080000
  //   34090001 340a0001 10a4020 1109fffe 1000ffff
endmodule

module PC (
  input  in_1,
  input  in_2,
  input  [31:0] in,
  output [31:0] out
);

  wire [31:0] PC_q, subtractor_1_out;

  Subtractor #(.width(32)) subtractor_1 (.a(in), .b(32'h3000), .out(subtractor_1_out));  // open: bin, bout
  Register #(.width(32)) PC (.D(subtractor_1_out), .Q(PC_q), .clk(in_2), .clr(in_1));  // open: en
  Adder #(.width(32)) adder_1 (.a(PC_q), .b(32'h3000), .out(out));  // open: cin, cout

  // Other names for the same wires on the sheet: clk = in_2; reset = in_1
endmodule

module EXT (
  input  [15:0] in_1,
  input  extOp,
  output [31:0] out_3
);

  wire [31:0] bit_extender_1_out, bit_extender_2_out;

  assign bit_extender_1_out = {{16{1'b0}}, in_1};  // Bit_Extender bit_extender_1
  assign bit_extender_2_out = {{16{in_1[15]}}, in_1};  // Bit_Extender bit_extender_2
  Multiplexer #(.width(32)) multiplexer_1 (
    .in0(bit_extender_1_out), .in1(bit_extender_2_out), .out(out_3), .sel(extOp));  // open: en
endmodule

module ALU (
  input  [2:0] ALUOp,
  input  [31:0] RD1,
  input  [31:0] RD2,
  output Zero,
  output [31:0] ALUout
);

  wire [31:0] adder_1_out, and_1_out, or_1_out, shifter_1_out, subtractor_1_out;

  Adder #(.width(32)) adder_1 (.a(RD1), .b(RD2), .out(adder_1_out));  // open: cin, cout
  Subtractor #(.width(32)) subtractor_1 (.a(RD1), .b(RD2), .out(subtractor_1_out));  // open: bin, bout
  assign and_1_out = RD1 & RD2;  // AND_Gate and_1, 32 bits wide
  assign or_1_out = RD1 | RD2;  // OR_Gate or_1, 32 bits wide
  Shifter #(.width(32)) shifter_1 (.in(RD2), .\dist (5'b10000), .out(shifter_1_out));
  Comparator #(.width(32), .mode("unsigned")) comparator_1 (.a(RD1), .b(RD2), .eq(Zero));  // open: gt, lt
  Multiplexer #(.select(3), .width(32)) multiplexer_1 (
    .in0(adder_1_out), .in1(subtractor_1_out), .in2(and_1_out), .in3(or_1_out), .in4(shifter_1_out),
    .out(ALUout), .sel(ALUOp));  // open: in5, in6, in7, en
  // Probe on ALUOp
endmodule

module DM (
  input  in_1,
  input  in_2,
  input  in_3,
  input  [31:0] addr,
  input  [31:0] WD,
  output [31:0] RD
);

  RAM #(.addrWidth(12), .dataWidth(32), .bus("separate")) ram_1 (
    .addr(addr[13:2]), .din(WD), .data(RD), .str(in_1), .clk(in_3), .clr(in_2));  // open: sel, ld

  // Other names for the same wires on the sheet: clk = in_3; DMWr = in_1; reset = in_2
endmodule

module ctrl (
  input  [5:0] Op,
  input  [5:0] func,
  output [2:0] ALUOp,
  output beq,
  output RFwr,
  output ExtOp,
  output Bsel,
  output j_jal,
  output [1:0] A3sel,
  output jal,
  output [2:0] NPCop,
  output jr,
  output [1:0] WDsel,
  output DMWr
);

  wire addu, and_1_out, and_2_out, and_3_out, and_4_out, j, lb, lh, lui, lw, not_1_out, not_2_out, not_3_out,
       not_4_out, not_5_out, not_6_out, not_7_out, not_8_out, not_9_out, not_10_out, not_11_out, not_12_out,
       ori, sb, sh, sll, subu;

  not not_1 (not_1_out, Op[4]);
  not not_2 (not_2_out, Op[5]);
  not not_3 (not_3_out, Op[3]);
  or or_1 (NPCop[0], jr, beq);
  or or_2 (NPCop[1], A3sel[1], jr);
  buf or_3 (NPCop[2], 1'b0);  // OR_Gate
  not not_4 (not_4_out, Op[2]);
  not not_5 (not_5_out, Op[1]);
  not not_6 (not_6_out, Op[0]);
  and special (A3sel[0], not_2_out, not_1_out, not_3_out, not_4_out, not_5_out, not_6_out);
  and u_lui (lui, not_2_out, not_1_out, Op[3], Op[2], Op[1], Op[0]);
  and u_ori (ori, not_2_out, not_1_out, Op[3], Op[2], not_5_out, Op[0]);
  and u_lw (lw, Op[5], not_1_out, not_3_out, not_4_out, Op[1], Op[0]);
  and sw (DMWr, Op[5], not_1_out, Op[3], not_4_out, Op[1], Op[0]);
  and u_beq (beq, not_2_out, not_1_out, not_3_out, Op[2], not_5_out, not_6_out);
  and u_j (j, not_2_out, not_1_out, not_3_out, not_4_out, Op[1], not_6_out);
  and u_lb (lb, Op[5], not_1_out, not_3_out, not_4_out, not_5_out, not_6_out);
  and u_lh (lh, Op[5], not_1_out, not_3_out, not_4_out, not_5_out, Op[0]);
  and u_sb (sb, Op[5], not_1_out, Op[3], not_4_out, not_5_out, not_6_out);
  and u_sh (sh, Op[5], not_1_out, Op[3], not_4_out, not_5_out, Op[0]);
  and u_jal (A3sel[1], not_2_out, not_1_out, not_3_out, not_4_out, Op[1], Op[0]);
  // AND_Gate and_1 has open pins: out=and_1_out
  // AND_Gate and_2 has open pins: out=and_2_out
  or or_4 (Bsel, lui, ori, lw, DMWr);
  or or_5 (WDsel[0], lw, lb);
  buf or_6 (WDsel[1], A3sel[1]);  // OR_Gate
  not not_7 (not_7_out, func[4]);
  not not_8 (not_8_out, func[5]);
  not not_9 (not_9_out, func[3]);
  not not_10 (not_10_out, func[1]);
  not not_11 (not_11_out, func[2]);
  buf or_7 (ALUOp[1], ori);  // OR_Gate
  not not_12 (not_12_out, func[0]);
  or or_8 (ALUOp[0], subu, ori);
  buf or_9 (ALUOp[2], lui);  // OR_Gate
  or or_10 (RFwr, addu, subu, lw, ori, lui);
  or or_11 (ExtOp, lw, DMWr, beq, lb);
  or or_12 (j_jal, j, A3sel[1]);
  and u_addu (addu, A3sel[0], func[5], not_7_out, not_9_out, not_11_out, not_10_out, not_12_out);
  and u_subu (subu, A3sel[0], func[5], not_7_out, not_9_out, not_11_out, func[1], not_12_out);
  and u_jr (jr, A3sel[0], not_8_out, not_7_out, func[3], not_11_out, not_10_out, not_12_out);
  and u_sll (sll, A3sel[0], not_8_out, not_7_out, not_9_out, not_11_out, not_10_out, not_12_out);
  buf and_3 (and_3_out, A3sel[0]);  // AND_Gate
  buf and_4 (and_4_out, A3sel[0]);  // AND_Gate

  assign jal = A3sel[1];

  // Other names for the same wires on the sheet: special = A3sel[0]; fun0 = func[0]; fun1 = func[1]; fun2 = func[2];
  //   fun3 = func[3]; fun4 = func[4]; fun5 = func[5]; sw = DMWr

  // Notes on the sheet:
  //   深绿代表1,浅绿代表0
  //   相当于ALU B操作数的来源
  //   0：RD2寄存器；1：imm
  //   R？R型指令op均为0，存到Rd
  //   01 mem->reg
  //   10 PC+4->reg
  //   GRF wd的来源
  //   00 ALUres->reg
endmodule
