// Logisim project ftoi.circ as structural Verilog: 3 circuits, main circuit ftoi
module ftoi (
  input  [15:0] in_1,
  output [31:0] out_2
);

  wire and_1_out, flg, not_1_out, or_1_out;
  wire [4:0] \移动x位 ;
  wire [15:0] \整数部分_1_out_3 ;
  wire [31:0] adder_1_out, bit_extender_1_out, multiplexer_1_out, not_2_out;

  \阶转补  \u_阶转补_1  (.in_1(in_1[14:10]), .out_2(\移动x位 ));
  // Probe on \移动x位 
  and and_1 (and_1_out, in_1[10], in_1[11], in_1[12], in_1[13], in_1[14]);
  or or_1 (or_1_out, in_1[10], in_1[11], in_1[12], in_1[13], in_1[14]);
  not not_1 (not_1_out, or_1_out);
  \整数部分  \u_整数部分_1  (.in_1(in_1[14:10]), .in_2(in_1[9:0]), .out_3(\整数部分_1_out_3 ));
  or or_2 (flg, and_1_out, not_1_out, \移动x位 [4]);
  assign bit_extender_1_out = {{16{1'b0}}, \整数部分_1_out_3 };  // Bit_Extender bit_extender_1
  assign not_2_out = ~bit_extender_1_out;  // NOT_Gate not_2, 32 bits wide
  Multiplexer #(.width(32)) multiplexer_1 (
    .in0(bit_extender_1_out), .in1(adder_1_out), .out(multiplexer_1_out), .sel(in_1[15]));  // open: en
  Adder #(.width(32)) adder_1 (.a(not_2_out), .b(32'h1), .out(adder_1_out));  // open: cin, cout
  Multiplexer #(.width(32)) multiplexer_2 (
    .in0(multiplexer_1_out), .in1({32{1'b0}}), .out(out_2), .sel(flg));  // open: en

  // Other names for the same wires on the sheet: frac[9:0] = in_1[9:0]; e[4:0] = in_1[14:10]; sgn = in_1[15]
endmodule

module \阶转补  (
  input  [4:0] in_1,
  output [4:0] out_2
);

  Subtractor #(.width(5)) subtractor_1 (.a(in_1), .b(5'b01111), .out(out_2));  // open: bin, bout
endmodule

module \整数部分  (
  input  [4:0] in_1,
  input  [9:0] in_2,
  output [15:0] out_3
);

  wire \补位 ;
  wire [3:0] bit_extender_1_out, subtractor_1_out;
  wire [4:0] \移动x位 ;

  or or_1 (\补位 , in_1[0], in_1[1], in_1[2], in_1[3], in_1[4]);
  Bit_Extender #(.in_width(5), .out_width(4)) bit_extender_1 (.in(\移动x位 ), .out(bit_extender_1_out));
  // Probe on bit_extender_1_out
  // Probe on {\补位 , in_2, {5{1'b0}}}
  Subtractor #(.width(4)) subtractor_1 (
    .a(4'b1111), .b(bit_extender_1_out), .out(subtractor_1_out));  // open: bin, bout
  // Probe on \移动x位 
  \阶转补  \u_阶转补_1  (.in_1(in_1), .out_2(\移动x位 ));
  // Probe on out_3
  Shifter #(.width(16), .shift("lr")) shifter_1 (.in({\补位 , in_2, {5{1'b0}}}), .\dist (subtractor_1_out), .out(out_3));
  // Probe on subtractor_1_out

  // Other names for the same wires on the sheet: frac[9:0] = in_2; e[4:0] = in_1
endmodule
