// Logisim project fsm.circ as structural Verilog: 3 circuits, main circuit fsm
module fsm (
  input  in_1,
  input  [1:0] in,
  output out_3
);

  wire clock_1_out;
  wire [1:0] multiplexer_1_out, register_1_q, \状态转移_1_out_3 ;

  \状态转移  \u_状态转移_1  (.state(register_1_q), .in(in), .out_3(\状态转移_1_out_3 ));
  Multiplexer #(.width(2), .enable("false")) multiplexer_1 (
    .in0(\状态转移_1_out_3 ), .in1(2'b00), .out(multiplexer_1_out), .sel(in_1));
  Register #(.width(2)) register_1 (.D(multiplexer_1_out), .Q(register_1_q), .clk(clock_1_out));  // open: en, clr
  Clock clock_1 (.out(clock_1_out));
  \状态输出  \u_状态输出_1  (.in(in), .state(register_1_q), .out_3(out_3));

  // Other names for the same wires on the sheet: reset = in_1
endmodule

module \状态输出  (
  input  [1:0] in,
  input  [1:0] state,
  output out_3
);

  wire comparator_1_eq, comparator_2_eq, comparator_3_eq, or_1_out;

  Comparator #(.width(2), .mode("unsigned")) comparator_1 (.a(state), .b(2'b10), .eq(comparator_1_eq));  // open: gt, lt
  Comparator #(.width(2), .mode("unsigned")) comparator_2 (.a(2'b00), .b(in), .eq(comparator_2_eq));  // open: gt, lt
  Comparator #(.width(2), .mode("unsigned")) comparator_3 (.a(in), .b(2'b10), .eq(comparator_3_eq));  // open: gt, lt
  or or_1 (or_1_out, comparator_2_eq, comparator_3_eq);
  and and_1 (out_3, or_1_out, comparator_1_eq);
endmodule

module \状态转移  (
  input  [1:0] state,
  input  [1:0] in,
  output [1:0] out_3
);

  wire and_1_out, and_2_out, and_3_out, and_4_out, and_5_out, not_1_out, not_2_out, not_3_out, not_4_out,
       not_5_out, not_6_out, not_7_out, not_8_out, not_9_out;

  not not_1 (not_1_out, state[1]);
  not not_2 (not_2_out, in[0]);
  not not_3 (not_3_out, state[0]);
  not not_4 (not_4_out, in[0]);
  not not_5 (not_5_out, state[1]);
  not not_6 (not_6_out, in[1]);
  not not_7 (not_7_out, in[1]);
  not not_8 (not_8_out, state[0]);
  not not_9 (not_9_out, in[0]);
  and and_1 (and_1_out, not_1_out, state[0], not_2_out);
  or or_1 (out_3[1], and_1_out, and_2_out);
  and and_2 (and_2_out, state[1], not_3_out, not_4_out);
  and and_3 (and_3_out, not_5_out, not_6_out, in[0]);
  and and_4 (and_4_out, state[0], not_7_out, in[0]);
  or or_2 (out_3[0], and_3_out, and_4_out, and_5_out);
  and and_5 (and_5_out, state[1], not_8_out, not_9_out);
endmodule
