// Logisim project navigation.circ as structural Verilog: 3 circuits, main circuit navigation
module navigation (
  input  [1:0] in_1,
  input  in_2,
  input  in_3,
  output out_4,
  output hit
);

  wire [3:0] register_1_q, \状态转移_1_out0 ;

  // Probe on register_1_q
  \状态转移  \u_状态转移_1  (
    .s3(register_1_q[3]), .s2(register_1_q[2]), .s1(register_1_q[1]), .s0(register_1_q[0]), .in1(in_1[1]),
    .in0(in_1[0]), .out3(\状态转移_1_out0 [3]), .out2(\状态转移_1_out0 [2]), .out1(\状态转移_1_out0 [1]),
    .out0(\状态转移_1_out0 [0]));
  // Probe on \状态转移_1_out0 
  Register #(.width(4)) register_1 (.D(\状态转移_1_out0 ), .Q(register_1_q), .clk(in_2), .clr(in_3));  // open: en
  \输出  \u_输出_1  (.in_1(register_1_q), .hit(hit), .arrive(out_4));

  // Other names for the same wires on the sheet: clk = in_2; dir[1:0] = in_1; reset = in_3
endmodule

module \状态转移  (
  input  s3,
  input  s2,
  input  s1,
  input  s0,
  input  in1,
  input  in0,
  output out3,
  output out2,
  output out1,
  output out0
);

  wire and_1_out, and_2_out, and_3_out, and_4_out, and_5_out, and_6_out, and_7_out, and_8_out, and_9_out,
       and_10_out, and_11_out, and_12_out, and_13_out, and_14_out, and_15_out, and_16_out, not_1_out,
       not_2_out, not_3_out, not_4_out, not_5_out, not_6_out, not_7_out, not_8_out, not_9_out, not_10_out,
       not_11_out, not_12_out, not_13_out, not_14_out, not_15_out, not_16_out, not_17_out, not_18_out,
       not_19_out, not_20_out, not_21_out, not_22_out, not_23_out, not_24_out, not_25_out, not_26_out,
       not_27_out, not_28_out, not_29_out, not_30_out, not_31_out, not_32_out, not_33_out, not_34_out,
       not_35_out, not_36_out, not_37_out, not_38_out, not_39_out, not_40_out;

  not not_1 (not_1_out, s2);
  not not_2 (not_2_out, s0);
  not not_3 (not_3_out, in1);
  not not_4 (not_4_out, s2);
  not not_5 (not_5_out, s1);
  not not_6 (not_6_out, s0);
  not not_7 (not_7_out, s2);
  not not_8 (not_8_out, s0);
  not not_9 (not_9_out, in0);
  not not_10 (not_10_out, s2);
  not not_11 (not_11_out, s2);
  not not_12 (not_12_out, in1);
  not not_13 (not_13_out, in0);
  not not_14 (not_14_out, s2);
  not not_15 (not_15_out, s0);
  not not_16 (not_16_out, in1);
  not not_17 (not_17_out, in0);
  not not_18 (not_18_out, s2);
  not not_19 (not_19_out, in1);
  not not_20 (not_20_out, s2);
  not not_21 (not_21_out, s1);
  not not_22 (not_22_out, in1);
  not not_23 (not_23_out, s2);
  not not_24 (not_24_out, in1);
  not not_25 (not_25_out, in0);
  not not_26 (not_26_out, s2);
  not not_27 (not_27_out, s0);
  not not_28 (not_28_out, in1);
  not not_29 (not_29_out, s2);
  not not_30 (not_30_out, s0);
  not not_31 (not_31_out, in0);
  not not_32 (not_32_out, s2);
  not not_33 (not_33_out, s2);
  not not_34 (not_34_out, s1);
  not not_35 (not_35_out, in1);
  not not_36 (not_36_out, in0);
  not not_37 (not_37_out, s2);
  not not_38 (not_38_out, s2);
  not not_39 (not_39_out, s2);
  not not_40 (not_40_out, in0);
  and and_1 (and_1_out, not_1_out, not_2_out, not_3_out, in0);
  and and_2 (and_2_out, not_4_out, not_5_out, not_6_out, in1);
  and and_3 (and_3_out, not_7_out, not_8_out, in1, not_9_out);
  and and_4 (and_4_out, not_10_out, s0, in1, in0);
  and and_5 (and_5_out, not_11_out, s1, s0, not_12_out, not_13_out);
  and and_6 (and_6_out, not_14_out, s1, not_15_out, not_16_out, not_17_out);
  and and_7 (and_7_out, not_18_out, s1, s0, not_19_out, in0);
  and and_8 (and_8_out, not_20_out, not_21_out, s0, not_22_out);
  and and_9 (and_9_out, not_23_out, s0, not_24_out, not_25_out);
  and and_10 (and_10_out, not_26_out, s1, not_27_out, not_28_out, in0);
  and and_11 (and_11_out, not_29_out, s1, not_30_out, in1, not_31_out);
  and and_12 (and_12_out, not_32_out, s1, s0, in1, in0);
  and and_13 (and_13_out, not_33_out, not_34_out, not_35_out, not_36_out);
  and and_14 (and_14_out, not_37_out, s0, in1, in0);
  and and_15 (and_15_out, not_38_out, s1, in1, in0);
  and and_16 (and_16_out, not_39_out, s1, s0, not_40_out);
  or or_1 (out3, and_1_out, and_2_out, and_3_out, and_4_out, and_5_out);
  or or_2 (out2, and_6_out, and_7_out);
  or or_3 (out1, and_8_out, and_9_out, and_10_out, and_11_out, and_12_out);
  or or_4 (out0, and_13_out, and_14_out, and_15_out, and_16_out);
endmodule

module \输出  (
  input  [3:0] in_1,
  output hit,
  output arrive
);

  and and_1 (hit, 1'b1, in_1[3]);
  and and_2 (arrive, 1'b1, in_1[2]);
endmodule
