// Logisim project swap.circ as structural Verilog: 4 circuits, main circuit 1bit_swap
module _1bit_swap (
  input  a,
  input  b,
  input  s,
  output out_4,
  output out_5
);

  wire and_1_out, and_2_out, and_3_out, and_4_out, not_1_out;

  not not_1 (not_1_out, s);
  and and_1 (and_1_out, a, not_1_out);
  and and_2 (and_2_out, b, s);
  and and_3 (and_3_out, a, s);
  and and_4 (and_4_out, b, not_1_out);
  or or_1 (out_4, and_1_out, and_2_out);
  or or_2 (out_5, and_3_out, and_4_out);
endmodule

module _4bit_swap (
  input  [3:0] in1,
  input  [3:0] in2,
  input  sel,
  output [3:0] out_4,
  output [3:0] out_5
);

  _1bit_swap u_1bit_swap_1 (.a(in1[0]), .b(in2[0]), .s(sel), .out_4(out_4[0]), .out_5(out_5[0]));
  _1bit_swap u_1bit_swap_2 (.a(in1[1]), .b(in2[1]), .s(sel), .out_4(out_4[1]), .out_5(out_5[1]));
  _1bit_swap u_1bit_swap_3 (.a(in1[2]), .b(in2[2]), .s(sel), .out_4(out_4[2]), .out_5(out_5[2]));
  _1bit_swap u_1bit_swap_4 (.a(in1[3]), .b(in2[3]), .s(sel), .out_4(out_4[3]), .out_5(out_5[3]));
endmodule

module _4bit_sort (
  input  [3:0] A,
  input  [3:0] B,
  input  [3:0] C,
  input  [3:0] D,
  output [3:0] _1,
  output [3:0] _2,
  output [3:0] _3,
  output [3:0] _4
);

  wire [3:0] tmp_1_out_3, tmp_1_out_4, tmp_2_out_3, tmp_2_out_4, tmp_3_out_3, tmp_4_out_3, tmp_4_out_4,
       tmp_5_out_3;

  tmp tmp_1 (.in_1(A), .in_2(B), .out_3(tmp_1_out_3), .out_4(tmp_1_out_4));
  tmp tmp_2 (.in_1(tmp_1_out_4), .in_2(C), .out_3(tmp_2_out_3), .out_4(tmp_2_out_4));
  tmp tmp_3 (.in_1(tmp_2_out_4), .in_2(D), .out_3(tmp_3_out_3), .out_4(_4));
  tmp tmp_4 (.in_1(tmp_1_out_3), .in_2(tmp_2_out_3), .out_3(tmp_4_out_3), .out_4(tmp_4_out_4));
  tmp tmp_5 (.in_1(tmp_4_out_4), .in_2(tmp_3_out_3), .out_3(tmp_5_out_3), .out_4(_3));
  tmp tmp_6 (.in_1(tmp_4_out_3), .in_2(tmp_5_out_3), .out_3(_1), .out_4(_2));
endmodule

module tmp (
  input  [3:0] in_1,
  input  [3:0] in_2,
  output [3:0] out_3,
  output [3:0] out_4
);

  wire comparator_1_gt;

  Comparator #(.width(4), .mode("unsigned")) comparator_1 (.a(in_1), .b(in_2), .gt(comparator_1_gt));  // open: eq, lt
  _4bit_swap u_4bit_swap_1 (.in1(in_1), .in2(in_2), .sel(comparator_1_gt), .out_4(out_3), .out_5(out_4));
endmodule
