// Logisim project 同步和异步.circ as structural Verilog: 1 circuit, main circuit main
module main (
  input  [1:0] \异步复位 ,
  input  in_2,
  input  [1:0] in_3,
  input  in_4,
  output [1:0] out_5,
  output [1:0] out_6
);

  wire clock_1_out, clock_2_out;
  wire [1:0] multiplexer_1_out;

  Register #(.width(2)) register_1 (.D(\异步复位 ), .Q(out_5), .clk(clock_1_out), .clr(in_2));  // open: en
  Clock clock_1 (.out(clock_1_out));
  Multiplexer #(.width(2), .enable("false")) multiplexer_1 (
    .in0(in_3), .in1(2'b00), .out(multiplexer_1_out), .sel(in_4));
  Register #(.width(2)) register_2 (.D(multiplexer_1_out), .Q(out_6), .clk(clock_2_out));  // open: en, clr
  Clock clock_2 (.out(clock_2_out));
endmodule
